# Fritzing sketch suitcase (saved by Fritzing 0.9.3b)
breadboards: 1

parts:
  part = Adafruit Ultimate GPS v3
  LTV2 = LTV847 [part_number=LTV847 package="DIP (Dual Inline) [THT]"]
  part_2 = Resistor [tolerance=±5% resistance=330 package=THT]
  part_3 = Resistor [tolerance=±5% resistance=330 package=THT]
  part_4 = Resistor [tolerance=±5% resistance=330 package=THT]
  part_5 = Resistor [tolerance=±5% resistance=330 package=THT]
  part_6 = Resistor [tolerance=±5% resistance=330 package=THT]
  part_7 = Resistor [tolerance=±5% resistance=330 package=THT]
  part_8 = Resistor [tolerance=±5% resistance=330 package=THT]
  part_9 = Resistor [tolerance=±5% resistance=330 package=THT]
  J9 = Terminal Block - 2 pins [package=THT]
  J10 = Terminal Block - 2 pins [package=THT]
  J11 = Terminal Block - 2 pins [package=THT]
  J12 = Terminal Block - 2 pins [package=THT]
  J13 = Terminal Block - 3 pins [package=THT]
  J16 = Terminal Block - 3 pins [package=THT]
  J14 = Terminal Block - 3 pins [package=THT]
  J15 = Terminal Block - 3 pins [package=THT]
  U1 = Mini-360 DC-DC Buck converter [package=THT]
  Tether_connector = IC, SIP package, 8 pins [chip_label="Binder 770"]
  Fathom-X_Tether_Interface_Board = IC, DIP package, 4 pins [chip_label="\nFathom-X Tether Interface Board"]
  USB2Serial = IC, SIP package, 4 pins [chip_label=USB2Serial]
  Ethernet_switch = IC, DIP package, 4 pins [chip_label=DGS-105]
  Echosounder = IC, SIP package, 4 pins [chip_label="Airmar DST800"]
  Mod1 = Raspberry Pi 4B

nets:
  N1: part.VIN, USB2Serial.pin3
  N2: part.GND, USB2Serial.pin4
  N3: part.RX, USB2Serial.pin2
  N4: part.TX, USB2Serial.pin1
  N5: LTV2.pin1, J12.Line_2, Echosounder.pin1
  N6: LTV2.pin2, part_3.Pin_1
  N7: LTV2.pin3, J11.Line_2, Echosounder.pin2
  N8: LTV2.pin4, part_8.Pin_1
  N9: LTV2.pin5, J10.Line_2
  N10: LTV2.pin6, part_9.Pin_1
  N11: LTV2.pin7, J9.Line_2
  N12: LTV2.pin8, part_4.Pin_1
  N13: LTV2.pin9, part_6.Pin_1, J16.Line_2
  N14: LTV2.pin10, J16.Line_3
  N15: LTV2.pin11, part_2.Pin_0, J15.Line_2
  N16: LTV2.pin12, J15.Line_3
  N17: LTV2.pin13, part_7.Pin_0, J14.Line_2, Mod1.GPIO15
  5 V: LTV2.pin14, LTV2.pin16, J13.Line_3, J14.Line_3, U1.OUT+, Ethernet_switch.pin1, Mod1.5V
  N18: LTV2.pin15, part_5.Pin_0, J13.Line_2, Mod1.GPIO14
  N19: part_2.Pin_1, J15.Line_1
  GND: part_3.Pin_0, part_5.Pin_1, part_7.Pin_1, part_8.Pin_0, J11.Line_1, J12.Line_1, J13.Line_1, J14.Line_1, U1.IN-, U1.OUT-, Tether_connector.pin4, Tether_connector.pin6, Tether_connector.pin8, Fathom-X_Tether_Interface_Board.pin2, Ethernet_switch.pin2, Echosounder.pin4, Mod1.GND
  N20: part_4.Pin_0, J9.Line_1
  N21: part_6.Pin_0, J16.Line_1
  N22: part_9.Pin_0, J10.Line_1
  12 V: U1.IN+, Fathom-X_Tether_Interface_Board.pin1, Echosounder.pin3
  N23: Tether_connector.pin1, Fathom-X_Tether_Interface_Board.pin4
  N24: Tether_connector.pin2, Fathom-X_Tether_Interface_Board.pin3
  48 V: Tether_connector.pin3, Tether_connector.pin5, Tether_connector.pin7

notes:
  - - - - - - - - - - - - - - - - - - - - - - - - - - - - - - - - - - - - - - - - - - - - - - - - - - - - - - - - - - - - - - - -
  - - - - - - - - - - - - - - - - - - - - - - - - - - - - - - - - - - - - - -
  Optocoupler

custom parts:
  Adafruit Ultimate GPS v3: We carry a few different GPS modules here in the Adafruit shop, but none that satisfied our every desire - that's why we designed this little GPS breakout board. We believe this is the Ultimate GPS module, so we named it that. It's got everything you want and more: -165 dBm sensitivity, 10 Hz updates, 66 channels 5V friendly design and only 20mA current draw Breadboard friendly + two mounting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
  LTV847: 4 opto-couplers
  Terminal Block - 2 pins: Generic Screw Terminal 8mm
  Terminal Block - 3 pins: Generic Screw Terminal 8mm
  Mini-360 DC-DC Buck converter: Mini-360 DC-DC Buck converter. Tiny buck step down voltage converter, input voltage 4.75 to 23V output 1 to 17V adjustable. Available from ebay and the like.
